# Fritzing sketch Untitled Sketch 3 (saved by Fritzing 0.9.3b)
perfboards: 1

parts:
  PIR1 = PIR sensor
  U1 = NodeMCU V3.0
  KY-1 = Keyes Relay [package=THT]
  J1 = Piezo Speaker
  J2 = Camdenboss CTB0158-3 [part_number=CTB0158-3 package=THT]
  HLK-PM1 = HLK-PM12 [part_number=HLK-PM12]
  J3 = Camdenboss CTB0158-2 [part_number=CTB0158-2 package=THT]  # not connected

nets:
  N1: PIR1.SIG, J2.pin2
  N2: U1.D7, KY-1.signal
  N3: U1.Vin, KY-1.power, HLK-PM1.+Vo
  N4: KY-1.ground, HLK-PM1.-Vo
  N5: KY-1.NO, J1.pin2

custom parts:
  NodeMCU V3.0: NodeMcu V3 Lua WIFI Development Board
  Keyes Relay: The Keyes 5V relay module is suitable for SCM development, home appliance control. It uses a 5V~12V TIL control signal which can control DC / AC signal.
